# Fritzing sketch blinkydesign (saved by Fritzing 0.9.2b)
circuit board: 8.46667cm x 5.64444cm
breadboards: 1

parts:
  TRINKET1 = Trinket 5V
  NEOPIXEL1 = Neopixel Strip -- White (30/m)
  S1 = Pushbutton [package="[SMD]"]
  C1 = Capacitor Polarized [package=panasonic_c]
  JACK1 = 2.1mm DC Barrel Jack

nets:
  N1: TRINKET1.no_name_yet#2, S1.Pin_3, S1.Pin_4
  N2: TRINKET1.no_name_yet#5, S1.Pin_1, S1.Pin_2
  N3: TRINKET1.no_name_yet#6, NEOPIXEL1.+5V#3, C1.+, JACK1.center
  N4: TRINKET1.no_name_yet#9, NEOPIXEL1.Din
  N5: NEOPIXEL1.GND, JACK1.switch
  N6: C1.-, JACK1.sleeve

custom parts:
  Trinket 5V: Adafruit Trinket 5V
  Neopixel Strip -- White (30/m): These NeoPixel strips have 30 digitally-addressable pixel LEDs per meter and are very affordable and are only 12.5 mm wide, 10 mm if you remove the strip from the casing.
  2.1mm DC Barrel Jack: 2.1mm DC Barrel Jack with Thru-Hole Connectors (breadboardable)
